// Logisim project ALU.circ as structural Verilog: 3 circuits, main circuit main
module main (
  input  [31:0] BusW,
  input  [2:0] RA,
  input  [2:0] RB,
  input  [2:0] RW,
  input  clear,
  input  CLK,
  input  RegWr,
  output [31:0] BusA,
  output [31:0] BusB
);

  wire and_1_out, decoder_1_out0, decoder_1_out1, decoder_1_out2, decoder_1_out3, decoder_1_out4,
       decoder_1_out5, decoder_1_out6, decoder_1_out7;
  wire [31:0] R1_q, R2_q, R3_q, R4_q, R5_q, R6_q, R7_q;

  Decoder #(.select(3), .enable("false")) decoder_1 (
    .out0(decoder_1_out0), .out1(decoder_1_out1), .out2(decoder_1_out2), .out3(decoder_1_out3),
    .out4(decoder_1_out4), .out5(decoder_1_out5), .out6(decoder_1_out6), .out7(decoder_1_out7), .sel(RW));
  Register #(.width(32)) R1 (.D(BusW), .en(decoder_1_out1), .Q(R1_q), .clk(and_1_out), .clr(clear));
  Register #(.width(32)) R2 (.D(BusW), .en(decoder_1_out2), .Q(R2_q), .clk(and_1_out), .clr(clear));
  Register #(.width(32)) R3 (.D(BusW), .en(decoder_1_out3), .Q(R3_q), .clk(and_1_out), .clr(clear));
  Register #(.width(32)) R4 (.D(BusW), .en(decoder_1_out4), .Q(R4_q), .clk(and_1_out), .clr(clear));
  Register #(.width(32)) R5 (.D(BusW), .en(decoder_1_out5), .Q(R5_q), .clk(and_1_out), .clr(clear));
  Register #(.width(32)) R6 (.D(BusW), .en(decoder_1_out6), .Q(R6_q), .clk(and_1_out), .clr(clear));
  Register #(.width(32)) R7 (.D(BusW), .en(decoder_1_out7), .Q(R7_q), .clk(and_1_out), .clr(clear));
  and and_1 (and_1_out, CLK, RegWr);
  Multiplexer #(.select(3), .width(32), .enable("false")) multiplexer_1 (
    .in0({32{1'b0}}), .in1(R1_q), .in2(R2_q), .in3(R3_q), .in4(R4_q), .in5(R5_q), .in6(R6_q), .in7(R7_q),
    .out(BusA), .sel(RA));
  Multiplexer #(.select(3), .width(32), .enable("false")) multiplexer_2 (
    .in0({32{1'b0}}), .in1(R1_q), .in2(R2_q), .in3(R3_q), .in4(R4_q), .in5(R5_q), .in6(R6_q), .in7(R7_q),
    .out(BusB), .sel(RB));
endmodule

module pc (
  input  Reset
);

  wire alu_1_out_6, alu_1_out_7, alu_1_out_8, ALUSrc, CLK, MemR, MemW, NOP, R7, RegW, SavePC, SignExt, WrData;
  wire [1:0] f, main_4_pcsrc;
  wire [2:0] main_1_a3, main_1_b3, main_1_d3, multiplexer_1_out, multiplexer_2_out;
  wire [4:0] main_1_imm5, OP;
  wire [5:0] main_5_out_3;
  wire [15:0] Instruction;
  wire [19:0] adder_1_out, adder_2_out, main_1_eximm11, multiplexer_4_out, NextPC, register_2_q;
  wire [31:0] alu_1_result, bit_extender_1_out, main_1_imm32, main_3_busa, main_3_busb, multiplexer_3_out,
       multiplexer_5_out, multiplexer_6_out, ram_1_data, register_1_q;

  Splitter_main main_1 (
    .InstCode(Instruction), .OP(OP), .a3(main_1_a3), .b3(main_1_b3), .d3(main_1_d3), .f(f),
    .ExImm11(main_1_eximm11), .CLK(CLK), .Imm32(main_1_imm32), .SignExt(SignExt), .NOP(NOP),
    .Imm5(main_1_imm5), .reset(Reset));
  MainCtrl_main main_2 (
    .OP(OP), .NOP(NOP), .SignExt(SignExt), .RegW(RegW), .SavePC(SavePC), .ALUSrc(ALUSrc), .WrData(WrData),
    .MemR(MemR), .MemW(MemW), .R7(R7));
  Multiplexer #(.width(3), .enable("false")) multiplexer_1 (
    .in0(main_1_b3), .in1(main_1_d3), .out(multiplexer_1_out), .sel(ALUSrc));
  Multiplexer #(.width(3), .enable("false")) multiplexer_2 (
    .in0(multiplexer_1_out), .in1(3'b111), .out(multiplexer_2_out), .sel(R7));
  assign bit_extender_1_out = {{12{1'b0}}, NextPC};  // Bit_Extender bit_extender_1
  Adder #(.width(20)) adder_1 (.a(main_1_imm32[19:0]), .b(register_2_q), .out(adder_1_out), .cin(1'b0));  // open: cout
  Adder #(.width(20)) adder_2 (.a(main_1_eximm11), .b(register_2_q), .out(adder_2_out), .cin(1'b0));  // open: cout
  main main_3 (
    .RA(main_1_a3), .RB(main_1_b3), .RW(multiplexer_2_out), .BusW(multiplexer_3_out), .BusA(main_3_busa),
    .BusB(main_3_busb), .CLK(CLK), .RegWr(RegW), .clear(Reset));
  Multiplexer #(.width(32), .enable("false")) multiplexer_3 (
    .in0(multiplexer_6_out), .in1(register_1_q), .out(multiplexer_3_out), .sel(SavePC));
  Register #(.width(32)) register_1 (.D(bit_extender_1_out), .en(1'b1), .Q(register_1_q), .clk(CLK), .clr(Reset));
  PCCtrl_main main_4 (.PCSrc(main_4_pcsrc), .OP(OP), .in_1(alu_1_out_7), .in_2(alu_1_out_8), .in_3(alu_1_out_6));
  Clock clock_1 (.out(CLK));
  Multiplexer #(.select(2), .width(20), .enable("false")) multiplexer_4 (
    .in0(NextPC), .in1(adder_1_out), .in2(adder_2_out), .in3(main_3_busa[19:0]), .out(multiplexer_4_out),
    .sel(main_4_pcsrc));
  Multiplexer #(.width(32), .enable("false")) multiplexer_5 (
    .in0(main_1_imm32), .in1(main_3_busb), .out(multiplexer_5_out), .sel(ALUSrc));
  ALUCtrl_main main_5 (.OP(OP), .out_3(main_5_out_3), .f(f));
  Adder #(.width(20)) adder_3 (.a(20'h1), .b(register_2_q), .out(NextPC), .cin(1'b0));  // open: cout
  Register #(.width(20), .trigger("falling")) register_2 (
    .D(multiplexer_4_out), .en(1'b1), .Q(register_2_q), .clk(CLK), .clr(Reset));
  ALU alu_1 (
    .out_8(alu_1_out_8), .Shift(main_1_imm5), .Result(alu_1_result), .B(multiplexer_5_out), .A(main_3_busa),
    .ALU_Op(main_5_out_3), .out_7(alu_1_out_7), .out_6(alu_1_out_6));
  ROM #(.addrWidth(20), .dataWidth(16)) rom_1 (.addr(register_2_q), .data(Instruction), .sel(1'b1));
  RAM #(.addrWidth(20), .dataWidth(32), .bus("separate")) ram_1 (
    .addr(alu_1_result[19:0]), .din(main_3_busb), .data(ram_1_data), .str(MemW), .sel(1'b1), .clk(CLK),
    .ld(MemR), .clr(Reset));
  Multiplexer #(.width(32), .enable("false")) multiplexer_6 (
    .in0(alu_1_result), .in1(ram_1_data), .out(multiplexer_6_out), .sel(WrData));

  // Notes on the sheet:
  //   contents of rom_1 (hex, n*v repeats v):
  //   3023 30e7 2967 2145 3986 45cd 4b8a 54af 5e6e 270 73d 18e 14f 94c 975 c7a a77 6382 6ba2 73c2 7be2
  //   8544 4*0 8d44 92a6 9be2 0 0 ad80 a862 a520 d940 e00a e80b f00c
endmodule

module ALU (
  input  [5:0] ALU_Op,
  input  [31:0] B,
  input  [31:0] A,
  input  [4:0] Shift,
  output [31:0] Result,
  output out_6,
  output out_7,
  output out_8
);

  wire [31:0] adder_1_out, and_1_out, and_2_out, bit_extender_1_out, bit_extender_2_out, multiplexer_1_out,
       multiplexer_2_out, not_1_out, or_1_out, shifter_1_out, shifter_2_out, shifter_3_out, shifter_4_out,
       subtractor_1_out, xor_1_out;

  assign and_1_out = B & A;  // AND_Gate and_1, 32 bits wide
  assign and_2_out = B & not_1_out;  // AND_Gate and_2, 32 bits wide
  assign not_1_out = ~A;  // NOT_Gate not_1, 32 bits wide
  assign or_1_out = B | A;  // OR_Gate or_1, 32 bits wide
  Comparator #(.width(32)) comparator_1 (.a(A), .b(B), .gt(out_6), .eq(out_7), .lt(out_8));
  assign xor_1_out = B ^ A;  // XOR_Gate xor_1, 32 bits wide
  Adder #(.width(32)) adder_1 (.a(B), .b(A), .out(adder_1_out), .cin(1'b0));  // open: cout
  Subtractor #(.width(32)) subtractor_1 (.a(B), .b(A), .out(subtractor_1_out), .bin(1'b0));  // open: bout
  Shifter #(.width(32)) shifter_1 (.in(A), .\dist (Shift), .out(shifter_1_out));
  Shifter #(.width(32), .shift("lr")) shifter_2 (.in(A), .\dist (Shift), .out(shifter_2_out));
  Shifter #(.width(32), .shift("ar")) shifter_3 (.in(A), .\dist (Shift), .out(shifter_3_out));
  Shifter #(.width(32), .shift("rr")) shifter_4 (.in(A), .\dist (Shift), .out(shifter_4_out));
  assign bit_extender_1_out = {{31{1'b0}}, out_7};  // Bit_Extender bit_extender_1
  assign bit_extender_2_out = {{31{1'b0}}, out_8};  // Bit_Extender bit_extender_2
  Multiplexer #(.select(3), .width(32), .enable("false")) multiplexer_1 (
    .in0(and_1_out), .in1(and_2_out), .in2(or_1_out), .in3(xor_1_out), .in4(adder_1_out),
    .in5(subtractor_1_out), .in6(bit_extender_1_out), .in7(bit_extender_2_out), .out(multiplexer_1_out),
    .sel(ALU_Op[2:0]));
  Multiplexer #(.select(2), .width(32), .enable("false")) multiplexer_2 (
    .in0(shifter_1_out), .in1(shifter_2_out), .in2(shifter_3_out), .in3(shifter_4_out),
    .out(multiplexer_2_out), .sel(ALU_Op[4:3]));
  Multiplexer #(.width(32), .enable("false")) multiplexer_3 (
    .in0(multiplexer_1_out), .in1(multiplexer_2_out), .out(Result), .sel(ALU_Op[5]));

  // Other names for the same wires on the sheet: AL_Type[2:0] = ALU_Op[2:0]; Shift_Type[1:0] = ALU_Op[4:3];
  //   AL_Shift = ALU_Op[5]
endmodule
