// Logisim project ALUCtrl.circ as structural Verilog: 1 circuit, main circuit main
module main (
  input  [1:0] f,
  input  [4:0] OP,
  output [5:0] out_3
);

  wire and_1_out, L_SW_out;
  wire [2:0] multiplexer_2_out;
  wire [2:2] not_1_out;

  and Shft (out_3[5], ~OP[4], OP[3], OP[2]);  // AND_Gate
  and and_1 (and_1_out, ~OP[4], ~OP[3], ~OP[2]);  // AND_Gate
  Multiplexer #(.width(3), .enable("false")) multiplexer_1 (
    .in0(multiplexer_2_out), .in1(3'b100), .out(out_3[2:0]), .sel(L_SW_out));
  and L_SW (L_SW_out, OP[4], ~OP[3], OP[2], ~OP[1]);  // AND_Gate
  not not_1 (not_1_out[2], OP[2]);
  Multiplexer #(.width(3), .enable("false")) multiplexer_2 (
    .in0({not_1_out[2], OP[1:0]}), .in1({OP[0], f}), .out(multiplexer_2_out), .sel(and_1_out));

  assign out_3[4:3] = OP[1:0];
endmodule
