// Logisim project MainCtrl.circ as structural Verilog: 1 circuit, main circuit main
module main (
  input  [4:0] OP,
  input  NOP,
  output RegW,
  output SavePC,
  output MemR,
  output MemW,
  output WrData,
  output ALUSrc,
  output SignExt,
  output R7
);

  wire and_1_out, Brch_out, JALR_out, not_2_out, or_1_out, or_2_out, R_out, SW_out;

  not not_1 (SignExt, and_1_out);
  and and_1 (and_1_out, ~OP[4], ~OP[3], OP[2]);  // AND_Gate
  and and_2 (RegW, ~NOP, or_1_out);  // AND_Gate
  or or_1 (or_1_out, not_2_out, WrData, or_2_out);
  not not_2 (not_2_out, OP[4]);
  and and_3 (SavePC, or_2_out, ~WrData);  // AND_Gate
  or or_2 (or_2_out, R7, JALR_out);
  and JAL (R7, OP[4], OP[3], OP[2], ~OP[1], OP[0]);  // AND_Gate
  and JALR (JALR_out, OP[4], OP[3], ~OP[2], OP[1], OP[0]);  // AND_Gate
  and and_4 (MemR, ~NOP, WrData);  // AND_Gate
  and and_5 (MemW, ~NOP, SW_out);  // AND_Gate
  and LW (WrData, OP[4], ~OP[3], OP[2], ~OP[1], ~OP[0]);  // AND_Gate
  and R (R_out, ~OP[4], ~OP[3], ~OP[2], ~OP[1]);  // AND_Gate
  and SW (SW_out, OP[4], ~OP[3], OP[2], ~OP[1], OP[0]);  // AND_Gate
  or or_3 (ALUSrc, R_out, Brch_out);
  and Brch (Brch_out, OP[4], ~OP[3], ~OP[2]);  // AND_Gate
endmodule
