// Logisim project PC.circ as structural Verilog: 1 circuit, main circuit main
module main (
  output [19:0] Address
);

  wire [19:0] adder_1_out, multiplexer_1_out;

  Multiplexer #(.select(2), .width(20), .enable("false")) multiplexer_1 (
    .in0(adder_1_out), .out(multiplexer_1_out));  // open: in1, in2, in3, sel
  Register #(.width(20)) register_1 (.D(multiplexer_1_out), .Q(Address));  // open: en, clk, clr
  Adder #(.width(20)) adder_1 (.a(20'h1), .b(Address), .out(adder_1_out));  // open: cin, cout
endmodule
