// Logisim project PCCtrl.circ as structural Verilog: 1 circuit, main circuit main
module main (
  input  in_1,
  input  in_2,
  input  in_3,
  input  [4:0] OP,
  output [1:0] PCSrc
);

  wire and_1_out, Branch_out, J_JAL_out, JALR_out, multiplexer_1_out, not_1_out, or_3_out;

  and Branch (Branch_out, OP[4], ~OP[3], ~OP[2]);  // AND_Gate
  and and_1 (and_1_out, Branch_out, multiplexer_1_out);
  or or_1 (PCSrc[1], J_JAL_out, JALR_out);
  and J_JAL (J_JAL_out, OP[4], OP[3], OP[2], ~OP[1]);  // AND_Gate
  or or_2 (PCSrc[0], and_1_out, JALR_out);
  and JALR (JALR_out, OP[4], OP[3], ~OP[2], OP[1]);  // AND_Gate
  Multiplexer #(.select(2), .enable("false")) multiplexer_1 (
    .in0(in_1), .in1(not_1_out), .in2(in_2), .in3(or_3_out), .out(multiplexer_1_out), .sel(OP[1:0]));
  not not_1 (not_1_out, in_1);
  or or_3 (or_3_out, in_1, in_3);
endmodule
