// Logisim project Splitter.circ as structural Verilog: 1 circuit, main circuit main
module main (
  input  [15:0] InstCode,
  input  reset,
  input  CLK,
  input  SignExt,
  output NOP,
  output [4:0] OP,
  output [2:0] a3,
  output [2:0] b3,
  output [4:0] Imm5,
  output [31:0] Imm32,
  output [2:0] d3,
  output [1:0] f,
  output [19:0] ExImm11
);

  wire and_1_out, and_2_out, and_3_out, and_4_out, I_Type, IMM;
  wire [1:1] and_6_out;
  wire [31:0] bit_extender_2_out, bit_extender_3_out, bit_extender_4_out, bit_extender_5_out;

  and u_IMM (IMM, InstCode[15], InstCode[14], InstCode[13], InstCode[12], ~InstCode[11]);  // AND_Gate
  Register #(.width(16)) register_1 (.D(InstCode), .en(1'b1), .Q({OP, a3, b3, d3, f}), .clk(CLK), .clr(reset));
  and and_1 (and_1_out, ~OP[4], ~OP[3], OP[2]);  // AND_Gate
  assign ExImm11 = {{9{a3[2]}}, {a3, b3, d3, f}};  // Bit_Extender bit_extender_1
  or u_I_Type (I_Type, and_1_out, and_3_out, and_2_out, and_4_out);
  and and_2 (and_2_out, OP[4], ~OP[3], ~OP[2]);  // AND_Gate
  and and_3 (and_3_out, ~OP[4], OP[3], ~OP[2]);  // AND_Gate
  and and_4 (and_4_out, OP[4], ~OP[3], OP[2]);  // AND_Gate
  and and_5 (NOP, OP[4], OP[3], OP[2], OP[1]);
  assign bit_extender_2_out = {{27{1'b0}}, {d3, f}};  // Bit_Extender bit_extender_2
  assign bit_extender_3_out = {{27{d3[2]}}, {d3, f}};  // Bit_Extender bit_extender_3
  assign bit_extender_4_out = {{16{1'b0}}, {InstCode[10:0], d3, f}};  // Bit_Extender bit_extender_4
  assign bit_extender_5_out = {{16{InstCode[10]}}, {InstCode[10:0], d3, f}};  // Bit_Extender bit_extender_5
  Multiplexer #(.select(2), .width(32), .enable("false")) multiplexer_1 (
    .in0(bit_extender_2_out), .in1(bit_extender_3_out), .in2(bit_extender_4_out), .in3(bit_extender_5_out),
    .out(Imm32), .sel({and_6_out[1], SignExt}));
  and and_6 (and_6_out[1], I_Type, IMM);

  assign Imm5 = {d3, f};

  // Other names for the same wires on the sheet: IMM11[10:0] = InstCode[10:0]

  // Notes on the sheet:
  //   Next Instruction
  //   Prev. Instruction
endmodule
