// Logisim project reg.circ as structural Verilog: 1 circuit, main circuit main
module main (
  input  [31:0] BusW,
  input  [2:0] RA,
  input  [2:0] RB,
  input  [2:0] RW,
  input  CLK,
  output [31:0] BusA,
  output [31:0] BusB
);

  wire decoder_1_out1, decoder_1_out2, decoder_1_out3, decoder_1_out4, decoder_1_out5, decoder_1_out6,
       decoder_1_out7;
  wire [31:0] R1_q, R2_q, R3_q, R4_q, R5_q, R6_q, R7_q;

  Decoder #(.select(3), .enable("false")) decoder_1 (
    .out1(decoder_1_out1), .out2(decoder_1_out2), .out3(decoder_1_out3), .out4(decoder_1_out4),
    .out5(decoder_1_out5), .out6(decoder_1_out6), .out7(decoder_1_out7), .sel(RW));  // open: out0
  Register #(.width(32)) R1 (.D(BusW), .en(decoder_1_out1), .Q(R1_q), .clk(CLK));  // open: clr
  Register #(.width(32)) R2 (.D(BusW), .en(decoder_1_out2), .Q(R2_q), .clk(CLK));  // open: clr
  Register #(.width(32)) R3 (.D(BusW), .en(decoder_1_out3), .Q(R3_q), .clk(CLK));  // open: clr
  Register #(.width(32)) R4 (.D(BusW), .en(decoder_1_out4), .Q(R4_q), .clk(CLK));  // open: clr
  Register #(.width(32)) R5 (.D(BusW), .en(decoder_1_out5), .Q(R5_q), .clk(CLK));  // open: clr
  Register #(.width(32)) R6 (.D(BusW), .en(decoder_1_out6), .Q(R6_q), .clk(CLK));  // open: clr
  Register #(.width(32)) R7 (.D(BusW), .en(decoder_1_out7), .Q(R7_q), .clk(CLK));  // open: clr
  Multiplexer #(.select(3), .width(32), .enable("false")) multiplexer_1 (
    .in0({32{1'b0}}), .in1(R1_q), .in2(R2_q), .in3(R3_q), .in4(R4_q), .in5(R5_q), .in6(R6_q), .in7(R7_q),
    .out(BusA), .sel(RA));
  Multiplexer #(.select(3), .width(32), .enable("false")) multiplexer_2 (
    .in0({32{1'b0}}), .in1(R1_q), .in2(R2_q), .in3(R3_q), .in4(R4_q), .in5(R5_q), .in6(R6_q), .in7(R7_q),
    .out(BusB), .sel(RB));
endmodule
